# Fritzing sketch ubuzzer_wiring (saved by Fritzing 0.9.3b)
stripboards: 1

parts:
  Composant1 = Arduino Nano (Rev3.0) (ICSP)
  R1 = Resistor [tolerance=±5% resistance=100 package="0603 [SMD]"]
  J1 = Piezo Speaker

nets:
  N1: Composant1.D9, J1.pin1
  N2: Composant1.D10, R1.Pin_0, R1.Pin_1, J1.pin2

notes:
  100Ω
